# Fritzing sketch GameWiiChuck (saved by Fritzing 0.9.2b)
breadboards: 2

parts:
  Composant1 = Arduino Uno (Rev3)
  Composant2 = Triple Axis Accelerometer Breakout - ADXL345
  LED1 = LED - 5mm [color="Yellow (595nm)" package="5 mm [THT]"]
  LED2 = LED - 5mm [color="Yellow (595nm)" package="5 mm [THT]"]
  LED3 = LED - 5mm [color="Green (570nm)" package="5 mm [THT]"]
  LED4 = LED - 5mm [color="Red (633nm)" package="5 mm [THT]"]
  R2 = Resistor [tolerance=±5% resistance=220 package=THT]
  R3 = Resistor [tolerance=±5% resistance=220 package=THT]
  R4 = Resistor [tolerance=±5% resistance=220 package=THT]
  R5 = Resistor [tolerance=±5% resistance=220 package=THT]
  LED5 = LED - 5mm [color="Red (633nm)" package="5 mm [THT]"]
  LED6 = LED - 5mm [color="Green (570nm)" package="5 mm [THT]"]
  R6 = Resistor [tolerance=±5% resistance=220 package=THT]
  R7 = Resistor [tolerance=±5% resistance=220 package=THT]

nets:
  N1: Composant1.A4/SDA, Composant2.SDA
  N2: Composant1.A5/SCL, Composant2.SCL
  N3: Composant1.D8, R7.Pin_1
  N4: Composant1.D9_PWM, R6.Pin_1
  N5: Composant1.D10_PWM/SS, R2.Pin_0
  N6: Composant1.D11_PWM/MOSI, R5.Pin_0
  N7: Composant1.D12/MISO, R4.Pin_0
  N8: Composant1.D13/SCK, R3.Pin_0
  5V: Composant1.5V, Composant2.VCC
  GND: Composant1.GND, Composant2.GND, LED1.cathode, LED3.cathode, LED4.cathode, LED5.cathode, LED6.cathode
  N9: LED1.anode, R4.Pin_1
  N10: LED2.anode, R5.Pin_1
  N11: LED4.anode, R3.Pin_1
  N12: LED5.anode, R6.Pin_0
  N13: LED6.anode, R7.Pin_0
